# Fritzing sketch MDPH2_on_UR10e_Wire_Diagram (saved by Fritzing 0.9.5d)

parts:
  Part2 = Arduino Nano (Rev3.0)
  PS2 = prefix0000 [part_number=S-350-60]
  LM2596_24v_to_12v_Stepdown_Converter1 = LM2596 step down module
  U2 = SWITCH-SPST-2 [package=r_sw_th]
  RY1 = SSR-40VA
  S4 = IPC5 [package="[THT]"]
  S2 = Inkbird ITC-100 Temp Controller [part_number="TACRACPS1X0404GY "]
  S5 = Connector [package="[THT]"]
  S6 = Connector [package="[THT]"]

nets:
  N1: Part2.RESET, Part2.GND, Part2.A1, Part2.A0, PS2.connector4, LM2596_24v_to_12v_Stepdown_Converter1.IN-, LM2596_24v_to_12v_Stepdown_Converter1.OUT-, S5.Pin_1, S5.Pin_2, S5.Pin_3, S5.Pin_4
  N2: Part2.VIN, LM2596_24v_to_12v_Stepdown_Converter1.OUT+
  N3: PS2.connector1, LM2596_24v_to_12v_Stepdown_Converter1.IN+
  N4: PS2.connector6, PS2.connector8, U2.Live_1, S4.Pin_1, S4.Pin_2, S2.pin_9, S6.Pin_3, S6.Pin_4
  N5: PS2.connector7, U2.Neutral_1, RY1.Pin_1, S4.Pin_3, S4.Pin_4, S2.pin_10
  N6: U2.Live_2, U2.Neutral_2, S6.Pin_1, S6.Pin_2
  N7: RY1.Pin_3, S2.pin_8
  N8: RY1.Pin_4, S2.pin_6

custom parts:
  LM2596 step down module: LM2596 DC-DC step down power supply module 3 A.
  SSR-40VA: SSR-40VA solid state relay.
  Connector: A generic pushbutton.
